# Fritzing sketch ArduinoIR (saved by Fritzing 0.9.6b)
breadboards: 2

parts:
  Composant1 = Arduino Uno (Rev3)
  Composant2 = Arduino Uno (Rev3)
  IR1 = TSOP312.., 314.. [package=THT]
  LED1 = LEDs [package=led10mm]
  R1 = Resistor [tolerance=±5% resistance=100 package="0603 [SMD]"]
  S1 = Momentary Switch [package=ksa_sealed_tac_switch]
  R2 = Resistor [tolerance=±5% resistance=10k package="0603 [SMD]"]
  LED2 = LEDs [package=led10mm]
  R3 = Resistor [tolerance=±5% resistance=2.2k package="0603 [SMD]"]
  LED3 = LEDs [package=led10mm]
  R4 = Resistor [tolerance=±5% resistance=2.2k package="0603 [SMD]"]
  S2 = Momentary Switch [package=ksa_sealed_tac_switch]
  R5 = Resistor [tolerance=±5% resistance=10k package="0603 [SMD]"]

nets:
  N1: Composant1.D2, R3.Pin_0
  N2: Composant1.D3_PWM, IR1.GND
  N3: Composant1.5V, IR1.Data
  N4: Composant1.GND, IR1.Vs, LED2.C
  N5: Composant2.D2, R4.Pin_0
  N6: Composant2.D3_PWM, R1.Pin_1
  N7: Composant2.D4, S1.4, R2.Pin_1
  N8: Composant2.D5_PWM, S2.4, R5.Pin_1
  N9: Composant2.5V, S1.2, S2.2
  N10: Composant2.GND, LED1.C, R2.Pin_0, LED3.A, R5.Pin_0
  N11: LED1.A, R1.Pin_0
  N12: LED2.A, R3.Pin_1
  N13: LED3.C, R4.Pin_1

notes:
  Infrared Receiver
  Infrared Emitter
